# Fritzing sketch Nagesh_sanitizermachine (saved by Fritzing 0.9.3b)
breadboards: 1

parts:
  CONTRAST_ADJ = Trimmer Potentiometer [maximum_resistance=10kΩ package=THT]
  part = Arduino Mega  # not connected
  Arduino_MEGA = Arduino Mega 2560 (Rev3)
  Part1 = MicroSD Card Module
  GLCD_128x1 = 128 x 64 Graphic LCD  # not connected
  hc-sr1 = hc-sr04
  M1 = DC Motor  # not connected
  L298N1 = L298N motor driver
  SP1 = SPEAKER [package=pcb_mount_speaker]

nets:
  GND: CONTRAST_ADJ.leg2, Arduino_MEGA.GND, Part1.GND, hc-sr1.GND, L298N1.connector14, SP1.+
  N1: Arduino_MEGA.D5_PWM, SP1.-
  VCC: Arduino_MEGA.5V, Part1.VCC, hc-sr1.VCC
  N2: Arduino_MEGA.D38, hc-sr1.Echo
  N3: Arduino_MEGA.D39, hc-sr1.Trig
  N4: Arduino_MEGA.D42, L298N1.connector13
  N5: Arduino_MEGA.D50, Part1.MISO
  N6: Arduino_MEGA.D51, Part1.MOSI
  N7: Arduino_MEGA.D52, Part1.SCK
  N8: Arduino_MEGA.D53, Part1.CS

notes:
  Upload code beforehand then make connections.
  1 VSS - GND
  2 VDD - 5V +
  3 V0 - (contrast)
  4 RS - 36
  5 R/W - 35
  6 E - 37
  7 DB0 - 22
  8 DB1 - 23
  9 DB2 - 24
  10 DB3 - 25
  11 DB4 - 26
  12 DB5 - 27
  13 DB6 - 28
  14 DB7 - 29
  15 CS1 - 33
  16 CS2 - 34
  17 RST - 5V +
  18 VOUT - ( contrast)
  19 BLA - 5V +
  20 BLK - GND
  Echo pin-D38
  Trigger pin-D39
